# Fritzing sketch Battery Management Circuit (saved by Fritzing 0.9.9b)
breadboards: 1

parts:
  R1 = Resistor [tolerance=±0.25% resistance=1800 power=0.12W package="0402 [SMD]"]
  U1 = LIPO-2000mAh [package=lipo-2000]
  U2 = LIPO-2000mAh [package=lipo-2000]
  U3 = LIPO-2000mAh [package=lipo-2000]
  R2 = Resistor [tolerance=±0.25% resistance=1300 power=0.12W package="0402 [SMD]"]
  Voltage_Meter = Arduino Nano (Rev3.0) (ICSP)

nets:
  N1: R1.Pin_0, R2.Pin_1, Voltage_Meter.A0
  N2: R1.Pin_1, U1.-
  N3: U1.+, U2.-
  N4: U2.+, U3.-
  N5: U3.+, R2.Pin_0, Voltage_Meter.GND
